# Fritzing sketch light-mixer-encoders (saved by Fritzing 0.9.10b)
breadboards: 1

parts:
  Part7 = Arduino Nano (Rev3.0) (ICSP)
  S1 = Toggle Switch [package=THT]
  BAT1 = Powerbank-DIY [package=battery-18650]
  OLED1 = OLED 128x64 I2C Monochrome Display GND-VDD
  NeoPixel1 = NeoPixel [part_number=WS2812B]
  RE4 = Rotary Encoder [package=THT]
  RE5 = Rotary Encoder [package=THT]
  RE6 = Rotary Encoder [package=THT]

nets:
  GND: Part7.GND, BAT1.GND, OLED1.GND, NeoPixel1.GND, RE4.GND, RE4.SW-1, RE5.GND, RE5.SW-1, RE6.GND, RE6.SW-1
  N1: Part7.D2, RE4.Pin-A
  N2: Part7.D3, RE4.Pin-B
  N3: Part7.D4, RE5.Pin-A
  N4: Part7.D5, RE5.Pin-B
  N5: Part7.D6, RE6.Pin-A
  N6: Part7.D7, RE6.Pin-B
  N7: Part7.D8, NeoPixel1.IN
  N8: Part7.D9, RE4.SW-2
  N9: Part7.D10, RE5.SW-2
  N10: Part7.D11/MOSI, RE6.SW-2
  VDD: Part7.5V, S1.COM, OLED1.VDD, NeoPixel1.VDD
  N11: Part7.A5, OLED1.SCK
  N12: Part7.A4, OLED1.SDA
  N13: S1.L1, BAT1.5V

custom parts:
  Powerbank-DIY: Powerbank-DIY (do it yourself) with one 18650 Li-ion battery cell and modded with dupont cables.
  OLED 128x64 I2C Monochrome Display GND-VDD: OLED 128x64 I2C Monochrome Display. Note: there are two variants of this part, this one is the GND VDD SCK SDA variant. The other is VDD GND SCK SDA. Make sure you select the part that matches your module as using the incorrect part will probably destroy your module! In addition the mounting holes are marked on silkscreen but not by default drilled. If you want drilled mounting holes, copy a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
  NeoPixel: Single unit of a NeoPixel, based on the bright RGB LED WS2812B. These ultra-bright LEDs have a constant-current driver cooked right into the LED package! The pixels are chainable - so you only need 1 pin/wire to control as many LEDs as you like.
  Rotary Encoder: Rotary Encoder with push button
